# Fritzing sketch quadrelay (saved by Fritzing 0.9.10b)

parts:
  Raspberry_Pi_1 = Raspberry Pi 3 [part_number=RPI-3-V1.2]
  A1 = 2 channel relay module [package=THT]
  J1 = 120V duplex outlet_1
  J2 = 120V duplex outlet_1
  J3 = Camdenboss CTB0158-2 [part_number=CTB0158-2 package=THT]
  J4 = Camdenboss CTB0158-3 [part_number=CTB0158-3 package=THT]

nets:
  N1: Raspberry_Pi_1.GIPO22, Raspberry_Pi_1.GIPO23, A1.Pin_30
  N2: Raspberry_Pi_1.GIPO10, Raspberry_Pi_1.GND, A1.Pin_29
  N3: Raspberry_Pi_1.GIPO9, Raspberry_Pi_1.GIPO25, A1.Pin_28
  N4: Raspberry_Pi_1.GIPO11, Raspberry_Pi_1.GIPO8, A1.Pin_27
  N5: A1.Pin_1, J2.N2
  N6: A1.Pin_2, A1.Pin_5, A1.Pin_8, A1.Pin_11, J4.pin1
  N7: A1.Pin_4, J2.N1
  N8: A1.Pin_7, J1.N2
  N9: A1.Pin_10, J1.N1
  N10: A1.Pin_14, A1.Pin_15
  N11: A1.Pin_17, A1.Pin_18
  N12: A1.Pin_20, A1.Pin_21
  N13: A1.Pin_23, A1.Pin_24
  N14: A1.Pin_25, J3.pin2
  N15: A1.Pin_26, J3.pin1
  N16: J1.H1, J1.H2, J2.H1, J2.H2, J4.pin2
  N17: J1.G, J2.G, J4.pin3

notes:
  5VDC
  - +
  120VAC
  L N FG
  1
  2
  3
  4

custom parts:
  2 channel relay module: 4 channel Relay Module 5V 12V 24V High and Low Level Trigger Relay Control With Optocoupler Two Way relays DC 5 V 12 V 24 V Volt.
  120V duplex outlet_1: 120V duplex outlet.
